# Fritzing sketch Scematic (saved by Fritzing 0.9.5d)
breadboards: 1

parts:
  U1 = NodeMCU V1.0
  R1 = Resistor [tolerance=±5% resistance=47 package=THT]
  R2 = Resistor [tolerance=±5% resistance=47 package=THT]
  M1 = DC Motor
  U2 = LIPO-2000mAh [package=lipo-2000]
  Q2 = npn-Powertransistor [package="TO220 [THT]"]
  Q3 = npn-Powertransistor [package="TO220 [THT]"]
  Q4 = npn-Powertransistor [package="TO220 [THT]"]
  Q5 = npn-Powertransistor [package="TO220 [THT]"]
  R4 = Resistor [tolerance=±5% resistance=47 package=THT]
  R6 = Resistor [tolerance=±5% resistance=47 package=THT]
  M2 = DC Motor

nets:
  N1: U1.D0, R1.Pin_1
  N2: U1.D1, R6.Pin_1
  GND: U1.GND, U2.-, Q3.emitter, Q5.emitter
  3.7V: U1.Vin, U2.+, Q2.collector, Q4.collector
  N3: R1.Pin_0, Q3.base
  N4: R2.Pin_0, Q2.base
  N5: R2.Pin_1, M1.pin_1, Q3.collector
  N6: M1.pin_2, Q2.emitter
  N7: Q4.base, R4.Pin_0
  N8: Q4.emitter, M2.pin_1
  N9: Q5.base, R6.Pin_0
  N10: Q5.collector, R4.Pin_1, M2.pin_2

custom parts:
  NodeMCU V1.0: ESP8266 based NodeMCU
